# Fritzing sketch lights (saved by Fritzing 0.9.2b)
breadboards: 1

parts:
  Part1 = Arduino Due (Rev2b)
  Q4 = MOSFET-NCHANNEL [package=to220v]
  Q5 = MOSFET-NCHANNEL [package=to220v]
  Q6 = MOSFET-NCHANNEL [package=to220v]
  U1 = Tri-Color LED SMD [package=led-tricolor-smd]

nets:
  N1: Part1.GND, Q4.S, Q5.S, Q6.S
  N2: Part1.D2_PWM, Q5.G
  N3: Part1.D3_PWM, Q4.G
  N4: Part1.D4_PWM/SS1, Q6.G
  N5: Q4.D, U1.GRN
  N6: Q5.D, U1.RED
  N7: Q6.D, U1.BLU
